# Fritzing sketch CircuitDiagram (saved by Fritzing 0.9.3b)

parts:
  RE1 = Rotary Encoder [package=THT]
  S1 = Pushbutton [package=THT]
  Grove1 = Grove OLED 128x96
  Raspberry_Pi_Zero1 = Raspberry Pi 3 [part_number=RPI-3-V1.2]

nets:
  N1: RE1.EncoderPinA, Raspberry_Pi_Zero1.GPIO16
  GND: RE1.EncoderPinC, S1.leg1, Grove1.GND, Raspberry_Pi_Zero1.GND
  N2: RE1.EncoderPinB, Raspberry_Pi_Zero1.GPIO20
  N3: S1.leg0, Raspberry_Pi_Zero1.GPIO21
  3V3: Grove1.VCC, Raspberry_Pi_Zero1.3v3, Raspberry_Pi_Zero1.3V3
  N4: Grove1.SDA, Raspberry_Pi_Zero1.GPIO2
  N5: Grove1.SCL, Raspberry_Pi_Zero1.GPIO3

notes:
  D+
  D-
  GND
  Switch (integrated into encoder)
